// Digital circuit BW8cpu.dig as structural Verilog
module BW8cpu (
  input  VCC,
  input  GND,
  input  nIRQ,
  input  nREQ,
  input  CLK,
  input  nRST,
  output [15:0] ADDR,
  output [7:0] DATA,
  output R_nW,
  output nACK,
  output nBRK
);

  wire a_dbus_a, a_dbus_l, a_lhs_a, a_rhs_a, addr_a, alu_dbus_a, b_dbus_a, b_dbus_l, b_lhs_a, b_rhs_a,
       c_dbus_a, c_dbus_l, c_lhs_a, c_rhs_a, count, d_dbus_a, d_dbus_l, d_lhs_a, d_rhs_a, dbus_a, dbus_l,
       dec_sp, dp_addr_a, dp_dbus_a, dp_dbus_l, dpi_dbus_a, e_addr_a, e_xfer_l, ir_dbus_l, isr_xfer_a,
       mem_dbus_a, mem_dbus_l, nclk, pc_addr_a, pc_inc, pc_xfer_a, pc_xfer_l, reg_pc, reg_sp, reg_x, reg_y,
       rst, rst_xfer_a, sp_addr_a, sp_dec, sp_inc, sp_xfer_a, sp_xfer_l, spi_xfer_a, sr_dbus_a, sr_dbus_l,
       t1_dbus_a, t1_dbus_l, t1_rhs_a, t2_dbus_a, t2_lhs_a, t_addr_a, t_inc, x_addr_a, x_dec, x_inc,
       x_xfer_a, x_xfer_l, xfer_a, xfer_l, y_addr_a, y_dec, y_inc, y_xfer_a, y_xfer_l;
  wire [4:0] alu_op, flags;
  wire [7:0] dbus, lhs, opcode, reg_a, reg_b, reg_c, reg_d, reg_dp, reg_t1, reg_t2, rhs;
  wire [15:0] addr_bus, xfer;

  // Probe on reg_a
  // Probe on reg_c
  // Probe on reg_dp
  // Probe on reg_t1
  // Probe on reg_t2
  // Probe on reg_pc
  // Probe on reg_x
  PowerSupply powersupply_1 (.VDD(VCC), .GND(GND));
  // Probe on reg_b
  // Probe on reg_d
  // Probe on opcode
  // Probe on flags
  // Probe on reg_sp
  // Probe on reg_y
  // Probe on xfer
  // Probe on dbus
  // Probe on ADDR
  // Probe on DATA
  // control_unit Control_Unit: pin names not known; wires that end beside it: nIRQ, opcode, flags, nREQ, CLK, nRST, dbus_a, dbus_l, alu_op, xfer_a, xfer_l, addr_a, count, dec_sp, nBRK, nclk, rst
  instruction_register Instruction_Register (
    .clk(CLK), .dbus(dbus), .dbus_load(ir_dbus_l), .clr(nRST), .opcode(opcode));
  memory_bridge Memory_Bridge (.dbus_assert(mem_dbus_a), .dbus_load(mem_dbus_l), .dbus(dbus), .mbus(DATA));
  constant_generator_8bit DP_Initial_Val (.dpi_dbus_assert(dpi_dbus_a), .DPi(8'h1), .dbus(dbus));
  alu Arithmetic___Logic_Unit_and_Status_Register (
    .ALU_OP(alu_op), .LOAD_SR_DBUS(sr_dbus_l), .ASSERT_SR_DBUS(sr_dbus_a), .CLK(CLK), .CLR(nRST), .LHS(lhs),
    .RHS(rhs), .ASSERT_ALU_DBUS(alu_dbus_a), .FLAGS(flags), .DBUS(dbus));  // open: q
  accumulator E_Accumulator__A___B (
    .addr_assert(e_addr_a), .xfer_load(e_xfer_l), .a_dbus_load(a_dbus_l), .b_dbus_load(b_dbus_l),
    .a_dbus_assert(a_dbus_a), .b_dbus_assert(b_dbus_a), .a_lhs_assert(a_lhs_a), .b_lhs_assert(b_lhs_a),
    .a_rhs_assert(a_rhs_a), .b_rhs_assert(b_rhs_a), .dbus(dbus), .xfer(xfer), .clk(CLK), .clr(nRST),
    .addr(addr_bus), .reg_a(reg_a), .reg_b(reg_b));
  general_purpose_register C_Register (
    .clk(CLK), .dbus_load(c_dbus_l), .dbus_assert(c_dbus_a), .lhs_assert(c_lhs_a), .rhs_assert(c_rhs_a),
    .clr(nRST), .dbus(dbus), .lhs(lhs), .rhs(rhs), .\reg (reg_c));
  direct_page_register DP___Temp_Register (
    .dbus(dbus), .clk(CLK), .clr(nRST), .rhs(rhs), .addr(ADDR), .assert_dp_addr(dp_addr_a),
    .assert_t1_dbus(t1_dbus_a), .assert_t1_rhs(t1_rhs_a), .assert_dp_dbus(dp_dbus_a),
    .load_t1_dbus(t1_dbus_l), .load_dp_dbus(dp_dbus_l), .load_t2_dbus(t1_dbus_l), .assert_t_addr(t_addr_a),
    .assert_t2_dbus(t2_dbus_a), .assert_t2_lhs(t2_lhs_a), .t_inc(t_inc), .reg_dp(reg_dp), .reg_t1(reg_t1),
    .reg_t2(reg_t2));
  general_purpose_register D_Register (
    .clk(CLK), .dbus_load(d_dbus_l), .dbus_assert(d_dbus_a), .lhs_assert(d_lhs_a), .rhs_assert(d_rhs_a),
    .clr(nRST), .dbus(dbus), .lhs(lhs), .rhs(rhs), .\reg (reg_d));
  // address_register Program_Counter: pin names not known; wires that end beside it: xfer, rst, pc_xfer_l, pc_addr_a, pc_xfer_a, pc_inc, 1'b1, CLK, ADDR, reg_pc
  // address_register Stack_Pointer: pin names not known; wires that end beside it: xfer, rst, sp_xfer_l, sp_addr_a, sp_xfer_a, sp_inc, sp_dec, CLK, ADDR, reg_sp
  // address_register X_Index: pin names not known; wires that end beside it: xfer, rst, x_xfer_l, x_addr_a, x_xfer_a, x_inc, x_dec, CLK, ADDR, reg_x
  // address_register Y_Index: pin names not known; wires that end beside it: xfer, rst, y_xfer_l, y_addr_a, y_xfer_a, y_inc, y_dec, CLK, ADDR, reg_y
  constant_generator_16bit RST_Vector_Lo__ISR_Vector_Lo__and_SP_Init_Val (
    .RSTv_Lo(16'h1), .ISRv_Lo(16'h1), .SPi(16'h1), .SPi_xfer_assert(spi_xfer_a),
    .RST_xfer_assert(rst_xfer_a), .ISR_xfer_assert(isr_xfer_a), .xfer(xfer));
  // bus_controller Bus_Controller: pin names not known; wires that end beside it: dbus_a, dbus_l, xfer_a, xfer_l, addr_a, CLK, count, dec_sp, nclk, alu_dbus_a, a_dbus_a, b_dbus_a, c_dbus_a, d_dbus_a, sr_dbus_a, dp_dbus_a, t1_dbus_a, t2_dbus_a, mem_dbus_l, a_dbus_l, b_dbus_l, c_dbus_l, d_dbus_l, sr_dbus_l, dp_dbus_l

  assign R_nW = 1'b0;

  // Other names for the same wires on the sheet: ack_addr_a = nACK; mbus[7:0] = DATA

  // Notes on the sheet:
  //   VCC: default 1
  //   nIRQ: default 1
  //   nREQ: default 1
  //   CLK: Hz: 6
  //   nRST: default 1
  //   External Pinout
endmodule
