// Digital circuit control_unit.dig as structural Verilog
module control_unit (
  input  [1:0] mode,
  input  irq,
  input  clk,
  input  [7:0] opcode,
  input  [4:0] flags,
  output [3:0] dbus_assert,
  output [3:0] dbus_load,
  output [4:0] alu_op,
  output [4:0] xfer_assert,
  output [2:0] xfer_load,
  output [2:0] addr_assert,
  output [2:0] count,
  output dec_sp,
  output rst_useq,
  output [1:0] m_tog,
  output brk_clk
);

  wire sequencer_p1, sequencer_p2, sequencer_p4, sequencer_p5, sequencer_p6;
  wire [2:0] t_state;
  wire [7:0] ucode_2_d, ucode_3_d, ucode_4_d, ucode_d;

  // _74193 sequencer: pin names not known; wires that end beside it: sequencer_p1, sequencer_p2, clk, sequencer_p4, sequencer_p5, sequencer_p6, rst_useq, 1'b1, 1'b1, 1'b0, t_state[0], t_state[1], t_state[2]
  // NotConnected on sequencer_p1
  // NotConnected on sequencer_p2
  // NotConnected on sequencer_p4
  // NotConnected on sequencer_p5
  // NotConnected on sequencer_p6
  EEPROM #(.AddrBits(19), .Bits(8)) ucode (
    .A({mode, irq, opcode, flags, t_state}), .CS(1'b1), .WE(1'b0), .OE(1'b1), .D(ucode_d));
  EEPROM #(.AddrBits(19), .Bits(8)) ucode_2 (
    .A({mode, irq, opcode, flags, t_state}), .CS(1'b1), .WE(1'b0), .OE(1'b1), .D(ucode_2_d));
  _74ls574 _74ls574_1 (.nOC(1'b0), .CLK(clk), .D(ucode_d), .VCC(1'b1), .GND(1'b0), .Q({dbus_load, dbus_assert}));
  _74ls574 _74ls574_2 (.nOC(1'b0), .CLK(clk), .D(ucode_2_d), .VCC(1'b1), .GND(1'b0), .Q({xfer_assert[2:0], alu_op}));
  EEPROM #(.AddrBits(19), .Bits(8)) ucode_3 (
    .A({mode, irq, opcode, flags, t_state}), .CS(1'b1), .WE(1'b0), .OE(1'b1), .D(ucode_3_d));
  EEPROM #(.AddrBits(19), .Bits(8)) ucode_4 (
    .A({mode, irq, opcode, flags, t_state}), .CS(1'b1), .WE(1'b0), .OE(1'b1), .D(ucode_4_d));
  _74ls574 _74ls574_3 (
    .nOC(1'b0), .CLK(clk), .D(ucode_3_d), .VCC(1'b1), .GND(1'b0),
    .Q({addr_assert, xfer_load, xfer_assert[4:3]}));
  _74ls574 _74ls574_4 (
    .nOC(1'b0), .CLK(clk), .D(ucode_4_d), .VCC(1'b1), .GND(1'b0),
    .Q({brk_clk, m_tog, rst_useq, dec_sp, count}));

  // Other names for the same wires on the sheet: brk = brk_clk; xa_3 = xfer_assert[3]; xa_4 = xfer_assert[4];
  //   xa_0 = xfer_assert[0]; xa_1 = xfer_assert[1]; xa_2 = xfer_assert[2];
  //   ucode_addr[18:0] = {mode, irq, opcode, flags, t_state}
endmodule
